# Fritzing sketch Arduino_Controller_Schematics (saved by Fritzing 0.9.3b)
breadboards: 1

parts:
  Part1 = Arduino Nano (Rev3.0) (ICSP)
  BUTTON1 = Pushbutton [package="[SMD]"]
  BUTTON2 = Pushbutton [package="[SMD]"]
  R1 = Resistor [tolerance=±5% resistance=10k package="0603 [SMD]"]
  R2 = Resistor [tolerance=±5% resistance=10k package="0603 [SMD]"]
  LED_BLUE = smd LED [color="Blue (525nm)" package="0805 [SMD]"]
  S1 = SPST Switch [package=switch-spst-smd-a]
  NORMALDE_BUNUN_LED_RING_OLMASI_GEREKIYOR_AMA_BU_PROGRAMDA_BULAMADIM_BUNUN_DETAYLARI_README_MD'DE = RGB LED - (4 legs) [package="5 mm [THT]"]
  R3 = Rotary Potentiometer (Small) [maximum_resistance=100kΩ package=THT]
  LED_GREEN = smd LED [color="Green (565nm)" package="0805 [SMD]"]
  R4 = Resistor [tolerance=±5% resistance=220 package=THT]
  LED_RED = smd LED [color="Red (633nm)" package="0805 [SMD]"]
  S2 = SPST Switch [package=switch-spst-smd-a]

nets:
  N1: Part1.GND, R1.Pin_1, R2.Pin_1, S1.O, R3.leg1, R4.Pin_1, S2.O
  N2: Part1.D3, S2.S
  N3: Part1.D4, NORMALDE_BUNUN_LED_RING_OLMASI_GEREKIYOR_AMA_BU_PROGRAMDA_BULAMADIM_BUNUN_DETAYLARI_README_MD'DE.green_cathode
  N4: Part1.D5, S1.P
  N5: Part1.D6, Part1.5V, BUTTON1.Pin_3, BUTTON1.Pin_4, S1.S, NORMALDE_BUNUN_LED_RING_OLMASI_GEREKIYOR_AMA_BU_PROGRAMDA_BULAMADIM_BUNUN_DETAYLARI_README_MD'DE.common_anode, R3.leg2
  N6: Part1.D7, BUTTON2.Pin_3, BUTTON2.Pin_4
  N7: Part1.D9, LED_BLUE.anode
  N8: Part1.D10, LED_GREEN.anode
  N9: Part1.A0, R3.wiper
  N10: Part1.D11/MOSI, LED_RED.anode
  N11: BUTTON1.Pin_1, BUTTON1.Pin_2, BUTTON2.Pin_1, BUTTON2.Pin_2, R1.Pin_0, R2.Pin_0
  N12: LED_BLUE.cathode, LED_GREEN.cathode, R4.Pin_0, LED_RED.cathode
  N13: NORMALDE_BUNUN_LED_RING_OLMASI_GEREKIYOR_AMA_BU_PROGRAMDA_BULAMADIM_BUNUN_DETAYLARI_README_MD'DE.blue_cathode, S2.P
