# Fritzing sketch Untitled Sketch (saved by Fritzing 0.9.3b)

parts:
  LCD = LCD-16X2 [package=lcd-16x2]
  MEGA = Arduino Mega 2560 (Rev3)
  HC05 = Bluetooth HC-05 Macho
  R1 = Resistor [tolerance=±5% resistance=2.2k package=THT]
  R2 = Resistor [tolerance=±5% resistance=2.2k package="0603 [SMD]"]
  R3 = Resistor [tolerance=±5% resistance=1k package="0603 [SMD]"]

nets:
  GND: LCD.VSS, LCD.R_W, LCD.K, MEGA.GND, HC05.GND, R1.Pin_0, R2.Pin_0
  VDD: LCD.VDD, LCD.A, MEGA.5V, HC05.VCC
  N1: LCD.VO, R1.Pin_1
  N2: LCD.RS, MEGA.D27
  N3: LCD.E, MEGA.D26
  N4: LCD.DB4, MEGA.D25
  N5: LCD.DB5, MEGA.D24
  N6: LCD.DB6, MEGA.D23
  N7: LCD.DB7, MEGA.D22
  N8: MEGA.D12_PWM, HC05.RXD
  N9: MEGA.D11_PWM, R3.Pin_1
  N10: HC05.TXD, R2.Pin_1, R3.Pin_0
